# Fritzing sketch Untitled Sketch (saved by Fritzing 0.9.3b)
breadboards: 1

parts:
  M1 = Stepper Motor - Bipolar
  Pololu_A1 = Pololu A4988 [package=SO16]
  Part1 = Arduino Nano (Rev3.0)
  S1 = Pushbutton [package="[SMD]"]
  S2 = Pushbutton [package="[SMD]"]
  S3 = Pushbutton [package="[SMD]"]
  R1 = Resistor [tolerance=±5% resistance=10k package=THT]
  R2 = Resistor [tolerance=±5% resistance=10k package=THT]
  R3 = Resistor [tolerance=±5% resistance=10k package=THT]
  LCD2 = LCD screen
  LCM1602_IIC2 = LCM1602 IIC [part_number="LCM1602 IIC" chip_label="LCM1602 IIC" package="DIP (Dual Inline) [THT]"]
  J1 = female pin header, 7 pins [form="♀ (female)"]

nets:
  N1: M1.A, Pololu_A1.2B
  N2: M1.C, Pololu_A1.2A
  N3: M1.B, Pololu_A1.1A
  N4: M1.D, Pololu_A1.1B
  N5: Pololu_A1.STEP, Part1.D3
  N6: Pololu_A1.DIR, Part1.D2
  N7: Pololu_A1.GND#14, Part1.VIN
  N8: Pololu_A1.VMOT, Part1.GND
  N9: S1.Pin_1, S1.Pin_2, R1.Pin_0, J1.pin1
  N10: S1.Pin_3, S1.Pin_4, S2.Pin_4, S3.Pin_3, S3.Pin_4, LCM1602_IIC2.VCC, J1.pin6
  N11: S2.Pin_1, S2.Pin_2, R2.Pin_0, J1.pin2
  N12: S3.Pin_1, S3.Pin_2, R3.Pin_0, J1.pin3
  N13: R1.Pin_1, R2.Pin_1, R3.Pin_1, LCM1602_IIC2.GND, J1.pin7
  VSS: LCD2.VSS, LCM1602_IIC2.VSS
  VDD: LCD2.VDD, LCM1602_IIC2.VDD
  N14: LCD2.V0, LCM1602_IIC2.V0
  N15: LCD2.RS, LCM1602_IIC2.RS
  N16: LCD2.R/W, LCM1602_IIC2.RW
  N17: LCD2.E, LCM1602_IIC2.E
  N18: LCD2.DB0, LCM1602_IIC2.D0
  N19: LCD2.DB1, LCM1602_IIC2.D1
  N20: LCD2.DB2, LCM1602_IIC2.D2
  N21: LCD2.DB3, LCM1602_IIC2.D3
  N22: LCD2.DB4, LCM1602_IIC2.D4
  N23: LCD2.DB5, LCM1602_IIC2.D5
  N24: LCD2.DB6, LCM1602_IIC2.D6
  N25: LCD2.DB7, LCM1602_IIC2.D7
  N26: LCD2.LED-, LCM1602_IIC2.A
  N27: LCD2.LED+, LCM1602_IIC2.K
  N28: LCM1602_IIC2.SDA, J1.pin5
  N29: LCM1602_IIC2.SCL, J1.pin4

notes:
  UP
  DOWN
  OK
  S1 - D7
  S2 - D8
  S3 - D9
  SC L- A5
  SDA- A4
  VCC - 5v
  GND- GND <module fritzingVersion="0.9.3b.04.19.5c895d327c44a3114e5fcc9d8260daf0cbb52806">
  <boundingRects>
  <boundingRect rect="-16 -107.85 419.849 19.493" name="Breadboard View"/>
  <boundingRect rect="0 0 0 0" name="Schematic View"/>
  <boundingRect rect="0 0 0 0" name="PCB View"/>
  </boundingRects>
  <instances>
  <instance moduleIdRef="BreadboardLogoTextModuleID" path=":/resources/parts/core/breadboardlogotext.fzp" modelIndex="85487066">
  <property value="TIDAL VOLUME : 1500.0" name="logo"/>
  <property value="#000000" name="color"/>
  <property value="118.49084369230769" name="width"/>
  <property value="5.5013606000000008" name="height"/>
  <property value="&lt;svg xmlns=&quot;http://www.w3.org/2000/svg&quot; height=&quot;0.216589in&quot; width=&quot;4.66499in&quot; viewBox=&quot;0 0 280 13&quot;>&#xa; &lt;g id=&quot;breadboard&quot;>&#xa; &lt;text font-family=&quot;Droid Sans&quot; id=&quot;label&quot; fill=&quot;#000000&quot; font-size=&quot;10&quot; text-anchor=&quot;middle&quot; x=&quot;140&quot; y=&quot;9&quot; xml:space=&quot;preserve&quot; stroke-width=&quot;0&quot;>TIDAL VOLUME : 1500.0&lt;/text>&#xa; &lt;/g>&#xa;&lt;/svg>&#xa;" name="shape"/>
  <property value=":/resources/parts/svg/core/breadboard/breadboardlogo.svg" name="lastfilename"/>
  <title>TXT7</title>
  <views>
  <breadboardView layer="breadboard">
  <geometry z="3.00043" x="-16" y="-107.85"/>
  </breadboardView>
  <schematicView layer="icon">
  <geometry z="0" x="364" y="-14.85"/>
  </schematicView>
  <pcbView layer="icon">
  <geometry z="0" x="133.409" y="10"/>
  </pcbView>
  </views>
  </instance>
  </instances>
  </module>
  FLOW RATE               : LOW
  TIDAL VOLUME        : 1500.0
  BPM                          : 15
  IE RATIO                   : 6:6
  e-vent_mark1

custom parts:
  LCD screen: A standard character display, usually with 2x16 characters. Comes in many colors.
  LCM1602 IIC: I2C-Module to use a 1602 or 2004 LCD on with the wire.h libory Serial LCD Modul
